// Logisim project CPU Assembly 2026.circ as structural Verilog: 1 circuit, main circuit main
// Reset
module main (
  input  count_en,
  input  oen,
  input  jump,
  input  [7:0] in_4,
  input  in_5,
  input  load_a,
  input  en_a,
  input  load,
  input  sub,
  input  add,
  input  en_alu,
  input  ram_in,
  input  load_b,
  input  ram_out,
  input  en_b,
  input  in_16,
  input  in_17,
  input  in_18,
  output OV
);

  wire alu2025_1_cout, clock, clock_1_out, main_7_sign_s0, reset;
  wire [3:0] main_2__4bit_data_out, main_7_bottom_s1, main_7_bottom_s2, main_7_bottom_s3, main_7_top_s1,
       main_7_top_s2, main_7_top_s3;
  wire [7:0] alu2025_1_contents, main_2_contents, main_3_bus, main_3_contents, main_4_contents,
       main_5_internal_content, main_6_internal_content;
  wire [23:0] main_7_status;

  Clock clock_1 (.out(clock_1_out));
  Button u_reset (.out(reset));
  Clock_Module_main main_1 (.Clock_In(clock_1_out), .Halt(in_18), .Clock_Out(clock));
  // Probe on main_3_bus
  // Probe on main_2_contents
  MAR_module_main main_2 (
    .load_in(load), .rst(reset), .clk(clock), .bus_datain(main_3_bus),
    ._4bit_data_out(main_2__4bit_data_out), .contents(main_2_contents));
  // Probe on main_3_contents
  ram_module_without_MAR_main main_3 (
    .data_in(main_3_bus), .oe(ram_out), .write(ram_in), .contents(main_3_contents), .bus(main_3_bus),
    .add_in(main_2__4bit_data_out), .clr(reset), .clk(clock));
  assign main_3_bus = in_5 ? in_4 : 8'bz;  // Controlled_Buffer controlled_buffer_1
  _7_Segment_Display u_7_segment_display_1 (.g(main_7_sign_s0));  // open: f, a, b, e, d, c, dp
  // Probe on main_4_contents
  PC_module_logi_based_main main_4 (
    .data_in(main_3_bus), .oen(oen), .rst(reset), .Overflow(OV), .bus(main_3_bus),
    .contents(main_4_contents), .counten(count_en), .nload(jump), .clk(clock));
  _8bit_reg_module_74_based_main main_5 (
    .internal_content(main_5_internal_content), .datain(main_3_bus), .loadn(load_a), .clk(clock),
    .rst(reset), .oe(en_a), .bus(main_3_bus));
  // Probe on main_5_internal_content
  // Probe on main_6_internal_content
  _8bit_reg_module_74_based_main main_6 (
    .internal_content(main_6_internal_content), .datain(main_3_bus), .loadn(load_b), .clk(clock),
    .rst(reset), .oe(en_b), .bus(main_3_bus));
  // Probe on main_7_status
  display_main main_7 (
    .loadn(in_16), .bus(main_3_bus), .rst(reset), .clk(clock), .TOP_S3(main_7_top_s3),
    .BOTTOM_S3(main_7_bottom_s3), .TOP_S2(main_7_top_s2), .BOTTOM_S2(main_7_bottom_s2), .MODE(in_17),
    .TOP_S1(main_7_top_s1), .BOTTOM_S1(main_7_bottom_s1), .SIGN_S0(main_7_sign_s0), .STATUS(main_7_status));  // open: SEG3, SEG2, SEG1
  _7_Segment_Display u_7_segment_display_2 (
    .g(main_7_top_s2[3]), .f(main_7_top_s2[2]), .a(main_7_top_s2[1]), .b(main_7_top_s2[0]),
    .e(main_7_bottom_s2[3]), .d(main_7_bottom_s2[2]), .c(main_7_bottom_s2[1]), .dp(main_7_bottom_s2[0]));
  _7_Segment_Display u_7_segment_display_3 (
    .g(main_7_top_s1[3]), .f(main_7_top_s1[2]), .a(main_7_top_s1[1]), .b(main_7_top_s1[0]),
    .e(main_7_bottom_s1[3]), .d(main_7_bottom_s1[2]), .c(main_7_bottom_s1[1]), .dp(main_7_bottom_s1[0]));
  // Probe on alu2025_1_contents
  // Probe on alu2025_1_cout
  ALU2025 alu2025_1 (
    .Cout(alu2025_1_cout), .OUTPUT(main_3_bus), .B(main_6_internal_content), .A(main_5_internal_content),
    .Sub_Cin(sub), .Add(add), .Mul(1'b0), .XOR(1'b0), .AND(1'b0), .OR(1'b0), .Bus_Enable(en_alu),
    .contents(alu2025_1_contents));
  _7_Segment_Display u_7_segment_display_4 (
    .g(main_7_top_s3[3]), .f(main_7_top_s3[2]), .a(main_7_top_s3[1]), .b(main_7_top_s3[0]),
    .e(main_7_bottom_s3[3]), .d(main_7_bottom_s3[2]), .c(main_7_bottom_s3[1]), .dp(main_7_bottom_s3[0]));
endmodule
