// Logisim project PC module.circ as structural Verilog: 1 circuit, main circuit main
module main (
  input  [7:0] data_in,
  input  OEN,
  input  jump,
  input  count_en,
  input  rst,
  output [7:0] contents,
  output Overflow,
  output [7:0] bus
);

  wire clock_1_out, not_1_out;

  not not_1 (not_1_out, jump);
  Clock clock_1 (.out(clock_1_out));
  Counter #(.width(4), .max('hf)) counter_1 (
    .load(not_1_out), .D(data_in[3:0]), .count(count_en), .Q(contents[3:0]), .carry(Overflow),
    .clk(clock_1_out), .clr(rst));
  assign bus[3:0] = OEN ? contents[3:0] : 4'bz;  // Controlled_Buffer controlled_buffer_1
  assign bus[7:4] = OEN ? 4'b0000 : 4'bz;  // Controlled_Buffer controlled_buffer_2

  assign contents[7:4] = 4'b0000;
endmodule
